// Logisim project cpu.circ as structural Verilog
module main (
  input  in_1,
  input  in_2
);

  wire add, addi, ALUinB, and_1_out, and_2_out, beqz, blt, clk, DMwe, eqz, I, J, j_t, jal, jr,
       keyboard_1_avail, ltz, lw, memorylatch_1_oe_latched, memorylatch_1_we_latched, N, not_1_out,
       not_2_out, not_4_out, O, or_1_out, Rdst, Rwe, sl, sr, sub, X;
  wire [2:0] multiplexer_3_out, multiplexer_6_out;
  wire [3:0] opcode;
  wire [6:0] bit_extender_1_out;
  wire [7:0] inpdata;
  wire [11:0] address;
  wire [14:0] alu_1_outputdata;
  wire [15:0] addex, dataout, immex, memorylatch_1_address_latched, memorylatch_1_data_in_latched,
       multiplexer_1_out, multiplexer_2_out, multiplexer_4_out, multiplexer_5_out, multiplexer_7_out,
       multiplexer_8_out, multiplexer_9_out, nextPC, PC_out16, readRs, registerfile_1_reg2contents,
       sixteenbitadder_1_result;

  Clock clock_1 (.out(clk));
  Multiplexer #(.width(16), .enable("false")) multiplexer_1 (
    .in0(multiplexer_5_out), .in1(nextPC), .out(multiplexer_1_out), .sel(jal));
  Multiplexer #(.width(16), .enable("false")) multiplexer_2 (
    .in0(multiplexer_1_out), .in1(dataout), .out(multiplexer_2_out), .sel(lw));
  Multiplexer #(.width(3), .enable("false")) multiplexer_3 (
    .in0(address[5:3]), .in1(address[8:6]), .out(multiplexer_3_out), .sel(Rdst));
  not not_1 (not_1_out, clk);
  Keyboard keyboard_1 (.clk(not_2_out), .re(I), .clr(in_2), .avail(keyboard_1_avail), .data(inpdata[6:0]));
  not not_2 (not_2_out, clk);
  Multiplexer #(.width(16), .enable("false")) multiplexer_4 (
    .in0(multiplexer_7_out), .in1(readRs), .out(multiplexer_4_out), .sel(jr));
  Multiplexer #(.width(16), .enable("false")) multiplexer_5 (
    .in0({ltz, alu_1_outputdata}), .in1({{8{1'b0}}, inpdata}), .out(multiplexer_5_out), .sel(I));
  Multiplexer #(.width(3), .enable("false")) multiplexer_6 (
    .in0(multiplexer_3_out), .in1(3'b111), .out(multiplexer_6_out), .sel(jal));
  sixteenbitadder sixteenbitadder_1 (.B(immex), .A(nextPC), .result(sixteenbitadder_1_result));  // open: sub, ovf
  not not_3 (inpdata[7], keyboard_1_avail);
  Multiplexer #(.width(16), .enable("false")) multiplexer_7 (
    .in0(multiplexer_8_out), .in1(addex), .out(multiplexer_7_out), .sel(J));
  singreg PC (.R(in_2), .C(not_1_out), .WE(1'b1), .in16(multiplexer_4_out), .out16(PC_out16));
  // Probe on inpdata[6:0]
  Multiplexer #(.width(16), .enable("false")) multiplexer_8 (
    .in0(nextPC), .in1(sixteenbitadder_1_result), .out(multiplexer_8_out), .sel(or_1_out));
  or or_1 (or_1_out, and_1_out, and_2_out);
  and and_1 (and_1_out, beqz, eqz);
  sixteenbitadder sixteenbitadder_2 (.B(16'h1), .A(PC_out16), .result(nextPC));  // open: sub, ovf
  nor nor_1 (eqz, readRs[15], readRs[14], readRs[13], readRs[12], readRs[11], readRs[10], readRs[9], readRs[8], readRs[7], readRs[6], readRs[5], readRs[4], readRs[3], readRs[2], readRs[1], readRs[0]);
  RegisterFile registerfile_1 (
    .clk(clk), .RWE(Rwe), .reset(in_2), .WriteData(multiplexer_2_out), .rd(multiplexer_6_out),
    .ReadReg1(address[11:9]), .ReadReg2(address[8:6]), .Reg1Contents(readRs),
    .Reg2Contents(registerfile_1_reg2contents));
  and and_2 (and_2_out, blt, ltz);
  TTY #(.rows(13), .cols(80)) tty_1 (.data(bit_extender_1_out), .clk(clk), .we(O), .clr(in_2));
  Bit_Extender #(.in_width(16), .out_width(7)) bit_extender_1 (.in(readRs), .out(bit_extender_1_out));
  // Probe on readRs
  // Probe on readRs
  Multiplexer #(.width(16), .enable("false")) multiplexer_9 (
    .in0(registerfile_1_reg2contents), .in1(immex), .out(multiplexer_9_out), .sel(ALUinB));
  ROM #(.addrWidth(16), .dataWidth(16)) rom_1 (.addr(PC_out16), .data({opcode, address}));
  // Probe on multiplexer_9_out
  ALU alu_1 (
    .InputData1(readRs), .InputData2(multiplexer_9_out), .shamt(address[2:0]), .OpType(opcode),
    .OutputData({ltz, alu_1_outputdata}));
  // Probe on {ltz, alu_1_outputdata}
  // Probe on opcode
  // Probe on address[11:9]
  Decoder #(.select(4)) decoder_1 (
    .out0(add), .out1(sub), .out2(addi), .out3(N), .out4(X), .out5(sl), .out6(sr), .out7(lw), .out8(DMwe),
    .out9(beqz), .out10(blt), .out11(j_t), .out12(jr), .out13(jal), .out14(I), .out15(O), .sel(opcode));  // open: en
  // Probe on address[2:0]
  // Probe on address[5:3]
  // Probe on address[8:6]
  not not_4 (not_4_out, clk);
  // Probe on address[5:0]
  // Probe on immex
  assign immex = {{10{address[5]}}, address[5:0]};  // Bit_Extender bit_extender_2
  assign addex = {{4{address[11]}}, address};  // Bit_Extender bit_extender_3
  memorylatch memorylatch_1 (
    .address({ltz, alu_1_outputdata}), .WE(DMwe), .clk(not_4_out), .data_in(registerfile_1_reg2contents),
    .address_latched(memorylatch_1_address_latched), .WE_latched(memorylatch_1_we_latched),
    .OE_latched(memorylatch_1_oe_latched), .data_in_latched(memorylatch_1_data_in_latched));
  or or_2 (J, j_t, jal);
  RAM #(.addrWidth(16), .dataWidth(16), .trigger("high"), .databus("bibus")) ram_1 (
    .addr(memorylatch_1_address_latched), .we(memorylatch_1_we_latched), .oe(memorylatch_1_oe_latched),
    .din(memorylatch_1_data_in_latched), .dout(dataout));
  or or_3 (Rwe, sr, sl, add, addi, lw, sub, N, X, jal, I);
  or or_4 (Rdst, addi, lw);
  or or_5 (ALUinB, addi, lw, DMwe);

  // Other names for the same wires on the sheet: immediate[5:0] = address[5:0]; shamt[2:0] = address[2:0];
  //   Rd[2:0] = address[5:3]; Rt[2:0] = address[8:6]; Rs[2:0] = address[11:9]; breq = beqz; brlt = blt; inp = I;
  //   Rfram = lw; oup = O; reset = in_2; sw = DMwe; WE = in_1

  // Notes on the sheet:
  //   contents of rom_1 (hex, n*v repeats v):
  //   2190 5c34 5c37 d005 903f 2042 d01a 2043 2141 2083 6219 a689 16a0 9807 d03c 9801 b013 2140 b015 2482
  //   b00a 9a01 d01a 2242 b008 903f 2dba 8c40 8c81 8cc2 8d03 8d44 8dc5 2140 5a2d 2b40 5a2d 2b40 5a29 2b40
  //   2b47 208a d03c 291e 2912 2b7f 8b00 2640 9201 b029 2a40 d044 7c40 7c81 7cc2 7d03 7d44 7dc5 2d86 ce00
  //   20ff 2300 18a0 26c1 a13d 983c 8a0 ce00 2dbe 8c40 8c81 0 7280 9403 f400 2241 b048 208a f400 7c40 7c81
  //   2d82 ce00
endmodule

module singreg (
  input  R,
  input  C,
  input  WE,
  input  [15:0] in16,
  output [15:0] out16
);

  wire and_2_out, and_3_out, myand;

  and and_1 (myand, WE, C);
  D_Flip_Flop d_ff_1 (.D(in16[0]), .clk(and_2_out), .Q(out16[0]), .reset(R));  // open: Qn, preset
  and and_2 (and_2_out, WE, C);
  D_Flip_Flop d_ff_2 (.D(in16[1]), .clk(and_3_out), .Q(out16[1]), .reset(R));  // open: Qn, preset
  and and_3 (and_3_out, WE, C);
  D_Flip_Flop d_ff_3 (.D(in16[2]), .clk(myand), .Q(out16[2]), .reset(R));  // open: Qn, preset
  D_Flip_Flop d_ff_4 (.D(in16[3]), .clk(myand), .Q(out16[3]), .reset(R));  // open: Qn, preset
  D_Flip_Flop d_ff_5 (.D(in16[4]), .clk(myand), .Q(out16[4]), .reset(R));  // open: Qn, preset
  D_Flip_Flop d_ff_6 (.D(in16[5]), .clk(myand), .Q(out16[5]), .reset(R));  // open: Qn, preset
  D_Flip_Flop d_ff_7 (.D(in16[6]), .clk(myand), .Q(out16[6]), .reset(R));  // open: Qn, preset
  D_Flip_Flop d_ff_8 (.D(in16[7]), .clk(myand), .Q(out16[7]), .reset(R));  // open: Qn, preset
  D_Flip_Flop d_ff_9 (.D(in16[8]), .clk(myand), .Q(out16[8]), .reset(R));  // open: Qn, preset
  D_Flip_Flop d_ff_10 (.D(in16[9]), .clk(myand), .Q(out16[9]), .reset(R));  // open: Qn, preset
  D_Flip_Flop d_ff_11 (.D(in16[10]), .clk(myand), .Q(out16[10]), .reset(R));  // open: Qn, preset
  D_Flip_Flop d_ff_12 (.D(in16[11]), .clk(myand), .Q(out16[11]), .reset(R));  // open: Qn, preset
  D_Flip_Flop d_ff_13 (.D(in16[12]), .clk(myand), .Q(out16[12]), .reset(R));  // open: Qn, preset
  D_Flip_Flop d_ff_14 (.D(in16[13]), .clk(myand), .Q(out16[13]), .reset(R));  // open: Qn, preset
  D_Flip_Flop d_ff_15 (.D(in16[14]), .clk(myand), .Q(out16[14]), .reset(R));  // open: Qn, preset
  D_Flip_Flop d_ff_16 (.D(in16[15]), .clk(myand), .Q(out16[15]), .reset(R));  // open: Qn, preset
  // Probe on out16[11]

  // Other names for the same wires on the sheet: clock = C; out1 = out16[0]; out2 = out16[1]; out3 = out16[2];
  //   out4 = out16[3]; out5 = out16[4]; out6 = out16[5]; out7 = out16[6]; out8 = out16[7]; out9 = out16[8];
  //   out10 = out16[9]; out11 = out16[10]; out12 = out16[11]; out13 = out16[12]; out14 = out16[13]; out15 = out16[14];
  //   out16_t = out16[15]; reset = R
endmodule

module RegisterFile (
  input  clk,
  input  RWE,
  input  reset,
  input  [15:0] WriteData,
  input  [2:0] rd,
  input  [2:0] ReadReg1,
  input  [2:0] ReadReg2,
  output [15:0] Reg1Contents,
  output [15:0] Reg2Contents
);

  wire and_1_out, and_2_out, and_3_out, and_4_out, and_5_out, and_6_out, and_7_out, and_8_out, d0, d1, d2,
       d3, d4, d5, d6, d7, r10, r11, r12, r13, r14, r15, r16, r17, r20, r21, r22, r23, r24, r25, r26, r27;
  wire [15:0] singreg_1_out16, singreg_2_out16, singreg_3_out16, singreg_4_out16, singreg_5_out16,
       singreg_6_out16, singreg_7_out16, singreg_8_out16;

  Decoder #(.select(3)) decoder_1 (
    .out0(d0), .out1(d1), .out2(d2), .out3(d3), .out4(d4), .out5(d5), .out6(d6), .out7(d7), .sel(rd));  // open: en
  Decoder #(.select(3)) decoder_2 (
    .out0(r10), .out1(r11), .out2(r12), .out3(r13), .out4(r14), .out5(r15), .out6(r16), .out7(r17),
    .sel(ReadReg1));  // open: en
  Decoder #(.select(3)) decoder_3 (
    .out0(r20), .out1(r21), .out2(r22), .out3(r23), .out4(r24), .out5(r25), .out6(r26), .out7(r27),
    .sel(ReadReg2));  // open: en
  and and_1 (and_1_out, d0, RWE);
  and and_2 (and_2_out, d1, RWE);
  and and_3 (and_3_out, d2, RWE);
  and and_4 (and_4_out, d3, RWE);
  singreg singreg_1 (.R(reset), .C(clk), .WE(and_1_out), .in16({16{1'b0}}), .out16(singreg_1_out16));
  singreg singreg_2 (.R(reset), .C(clk), .WE(and_3_out), .in16(WriteData), .out16(singreg_2_out16));
  singreg singreg_3 (.R(reset), .C(clk), .WE(and_4_out), .in16(WriteData), .out16(singreg_3_out16));
  // Probe on singreg_1_out16
  assign Reg1Contents = r10 ? singreg_1_out16 : 16'bz;  // Controlled_Buffer controlled_buffer_1
  assign Reg2Contents = r20 ? singreg_1_out16 : 16'bz;  // Controlled_Buffer controlled_buffer_2
  // Probe on singreg_4_out16
  singreg singreg_4 (.R(reset), .C(clk), .WE(and_2_out), .in16(WriteData), .out16(singreg_4_out16));
  // Probe on singreg_2_out16
  assign Reg1Contents = r12 ? singreg_2_out16 : 16'bz;  // Controlled_Buffer controlled_buffer_3
  assign Reg2Contents = r22 ? singreg_2_out16 : 16'bz;  // Controlled_Buffer controlled_buffer_4
  // Probe on singreg_3_out16
  assign Reg1Contents = r13 ? singreg_3_out16 : 16'bz;  // Controlled_Buffer controlled_buffer_5
  assign Reg2Contents = r23 ? singreg_3_out16 : 16'bz;  // Controlled_Buffer controlled_buffer_6
  assign Reg1Contents = r11 ? singreg_4_out16 : 16'bz;  // Controlled_Buffer controlled_buffer_7
  assign Reg2Contents = r21 ? singreg_4_out16 : 16'bz;  // Controlled_Buffer controlled_buffer_8
  and and_5 (and_5_out, d4, RWE);
  and and_6 (and_6_out, d5, RWE);
  and and_7 (and_7_out, d6, RWE);
  and and_8 (and_8_out, d7, RWE);
  // Probe on singreg_5_out16
  singreg singreg_5 (.R(reset), .C(clk), .WE(and_6_out), .in16(WriteData), .out16(singreg_5_out16));
  singreg singreg_6 (.R(reset), .C(clk), .WE(and_7_out), .in16(WriteData), .out16(singreg_6_out16));
  // Probe on singreg_7_out16
  singreg singreg_7 (.R(reset), .C(clk), .WE(and_8_out), .in16(WriteData), .out16(singreg_7_out16));
  // Probe on singreg_8_out16
  assign Reg1Contents = r14 ? singreg_8_out16 : 16'bz;  // Controlled_Buffer controlled_buffer_9
  singreg singreg_8 (.R(reset), .C(clk), .WE(and_5_out), .in16(WriteData), .out16(singreg_8_out16));
  assign Reg2Contents = r24 ? singreg_8_out16 : 16'bz;  // Controlled_Buffer controlled_buffer_10
  assign Reg1Contents = r15 ? singreg_5_out16 : 16'bz;  // Controlled_Buffer controlled_buffer_11
  assign Reg2Contents = r25 ? singreg_5_out16 : 16'bz;  // Controlled_Buffer controlled_buffer_12
  // Probe on singreg_6_out16
  assign Reg1Contents = r16 ? singreg_6_out16 : 16'bz;  // Controlled_Buffer controlled_buffer_13
  assign Reg2Contents = r26 ? singreg_6_out16 : 16'bz;  // Controlled_Buffer controlled_buffer_14
  assign Reg1Contents = r17 ? singreg_7_out16 : 16'bz;  // Controlled_Buffer controlled_buffer_15
  assign Reg2Contents = r27 ? singreg_7_out16 : 16'bz;  // Controlled_Buffer controlled_buffer_16

  // Other names for the same wires on the sheet: output1[15:0] = Reg1Contents; output2[15:0] = Reg2Contents
endmodule

module ALU (
  input  [15:0] InputData1,
  input  [15:0] InputData2,
  input  [2:0] shamt,
  input  [3:0] OpType,
  output [15:0] OutputData
);

  wire [15:0] add, N, shl, shr, sub, X;

  // Probe on InputData1
  // Probe on InputData2
  // Probe on InputData1
  // Probe on InputData2
  assign N = ~InputData1;  // NOT_Gate not_1, 16 bits wide
  assign X = InputData1 ^ InputData2;  // XOR_Gate xor_1, 16 bits wide
  sixteenbitadder sixteenbitadder_1 (.sub(1'b1), .B(InputData2), .A(InputData1), .result(sub));  // open: ovf
  sixteenbitadder sixteenbitadder_2 (.sub(1'b0), .B(InputData1), .A(InputData2), .result(add));  // open: ovf
  barrelleftshift barrelleftshift_1 (.shamt(shamt), .inputreg(InputData1), .outreg(shl));
  barrelright barrelright_1 (.shamt(shamt), .inputreg(InputData1), .outreg(shr));
  // Probe on add
  Multiplexer #(.select(4), .width(16), .enable("false")) multiplexer_1 (
    .in0(add), .in1(sub), .in2(add), .in3(N), .in4(X), .in5(shl), .in6(shr), .in7(add), .in8(add), .in9(sub),
    .in10(sub), .out(OutputData), .sel(OpType));  // open: in11, in12, in13, in14, in15

  // Other names for the same wires on the sheet: In1[15:0] = InputData1; In2[15:0] = InputData2
endmodule

module onebitadder (
  input  Cin,
  input  A,
  input  B,
  output sum,
  output Cout
);

  wire and_1_out, and_2_out, xor_1_out;

  and and_1 (and_1_out, B, A);
  xor xor_1 (xor_1_out, A, B);
  or or_1 (Cout, and_1_out, and_2_out);
  and and_2 (and_2_out, xor_1_out, Cin);
  xor xor_2 (sum, Cin, xor_1_out);
endmodule

module sixteenbitadder (
  input  sub,
  input  [15:0] B,
  input  [15:0] A,
  output ovf,
  output [15:0] result
);

  wire Cout1, Cout2, Cout3, Cout4, Cout5, Cout6, Cout7, Cout8, Cout9, Cout10, Cout11, Cout12, Cout13, Cout14,
       Cout15, Cout16, xor_2_out, xor_3_out, xor_4_out, xor_5_out, xor_6_out, xor_7_out, xor_8_out,
       xor_9_out, xor_10_out, xor_11_out, xor_12_out, xor_13_out, xor_14_out, xor_15_out, xor_16_out,
       xor_17_out;

  xor xor_1 (ovf, Cout15, Cout16);
  onebitadder onebitadder_1 (.Cin(Cout15), .A(A[15]), .B(xor_2_out), .sum(result[15]), .Cout(Cout16));
  xor xor_2 (xor_2_out, sub, B[15]);
  onebitadder onebitadder_2 (.Cin(Cout14), .A(A[14]), .B(xor_3_out), .sum(result[14]), .Cout(Cout15));
  xor xor_3 (xor_3_out, sub, B[14]);
  onebitadder onebitadder_3 (.Cin(Cout13), .A(A[13]), .B(xor_4_out), .sum(result[13]), .Cout(Cout14));
  xor xor_4 (xor_4_out, sub, B[13]);
  onebitadder onebitadder_4 (.Cin(Cout12), .A(A[12]), .B(xor_5_out), .sum(result[12]), .Cout(Cout13));
  xor xor_5 (xor_5_out, sub, B[12]);
  onebitadder onebitadder_5 (.Cin(Cout11), .A(A[11]), .B(xor_6_out), .sum(result[11]), .Cout(Cout12));
  xor xor_6 (xor_6_out, sub, B[11]);
  onebitadder onebitadder_6 (.Cin(Cout10), .A(A[10]), .B(xor_7_out), .sum(result[10]), .Cout(Cout11));
  xor xor_7 (xor_7_out, sub, B[10]);
  onebitadder onebitadder_7 (.Cin(Cout9), .A(A[9]), .B(xor_8_out), .sum(result[9]), .Cout(Cout10));
  xor xor_8 (xor_8_out, sub, B[9]);
  onebitadder onebitadder_8 (.Cin(Cout8), .A(A[8]), .B(xor_9_out), .sum(result[8]), .Cout(Cout9));
  xor xor_9 (xor_9_out, sub, B[8]);
  onebitadder onebitadder_9 (.Cin(Cout7), .A(A[7]), .B(xor_10_out), .sum(result[7]), .Cout(Cout8));
  xor xor_10 (xor_10_out, sub, B[7]);
  onebitadder onebitadder_10 (.Cin(Cout6), .A(A[6]), .B(xor_11_out), .sum(result[6]), .Cout(Cout7));
  xor xor_11 (xor_11_out, sub, B[6]);
  onebitadder onebitadder_11 (.Cin(Cout5), .A(A[5]), .B(xor_12_out), .sum(result[5]), .Cout(Cout6));
  xor xor_12 (xor_12_out, sub, B[5]);
  onebitadder onebitadder_12 (.Cin(Cout4), .A(A[4]), .B(xor_13_out), .sum(result[4]), .Cout(Cout5));
  xor xor_13 (xor_13_out, sub, B[4]);
  onebitadder onebitadder_13 (.Cin(Cout3), .A(A[3]), .B(xor_14_out), .sum(result[3]), .Cout(Cout4));
  xor xor_14 (xor_14_out, sub, B[3]);
  onebitadder onebitadder_14 (.Cin(Cout2), .A(A[2]), .B(xor_15_out), .sum(result[2]), .Cout(Cout3));
  xor xor_15 (xor_15_out, sub, B[2]);
  onebitadder onebitadder_15 (.Cin(Cout1), .A(A[1]), .B(xor_16_out), .sum(result[1]), .Cout(Cout2));
  xor xor_16 (xor_16_out, sub, B[1]);
  onebitadder onebitadder_16 (.Cin(sub), .A(A[0]), .B(xor_17_out), .sum(result[0]), .Cout(Cout1));
  xor xor_17 (xor_17_out, sub, B[0]);

  // Other names for the same wires on the sheet: a1 = A[0]; a2 = A[1]; a3 = A[2]; a4 = A[3]; a5 = A[4]; a6 = A[5];
  //   a7 = A[6]; a8 = A[7]; a9 = A[8]; a10 = A[9]; a11 = A[10]; a12 = A[11]; a13 = A[12]; a14 = A[13]; a15 = A[14];
  //   a16 = A[15]; b1 = B[0]; b2 = B[1]; b3 = B[2]; b4 = B[3]; b5 = B[4]; b6 = B[5]; b7 = B[6]; b8 = B[7]; b9 = B[8];
  //   b10 = B[9]; b11 = B[10]; b12 = B[11]; b13 = B[12]; b14 = B[13]; b15 = B[14]; b16 = B[15]; sum1 = result[0];
  //   sum2 = result[1]; sum3 = result[2]; sum4 = result[3]; sum5 = result[4]; sum6 = result[5]; sum7 = result[6];
  //   sum8 = result[7]; sum9 = result[8]; sum10 = result[9]; sum11 = result[10]; sum12 = result[11];
  //   sum13 = result[12]; sum14 = result[13]; sum15 = result[14]; sum16 = result[15]
endmodule

module shiftleft (
  input  [15:0] rs,
  output [15:0] slout
);

  wire multiplexer_1_out, multiplexer_2_out, multiplexer_3_out, multiplexer_4_out, multiplexer_5_out,
       multiplexer_6_out, multiplexer_7_out, multiplexer_8_out, multiplexer_9_out, multiplexer_10_out,
       multiplexer_11_out, multiplexer_12_out, multiplexer_13_out, multiplexer_14_out, multiplexer_15_out,
       multiplexer_16_out, multiplexer_17_out, multiplexer_18_out, multiplexer_19_out, multiplexer_20_out,
       multiplexer_21_out, multiplexer_22_out, multiplexer_23_out, multiplexer_24_out, multiplexer_25_out,
       multiplexer_26_out, multiplexer_27_out, multiplexer_28_out, multiplexer_29_out, multiplexer_30_out,
       multiplexer_31_out;

  Multiplexer #(.enable("false")) multiplexer_1 (.in0(rs[15]), .in1(rs[14]), .out(multiplexer_1_out));  // open: sel
  Multiplexer #(.enable("false")) multiplexer_2 (.in0(rs[14]), .in1(rs[13]), .out(multiplexer_2_out));  // open: sel
  Multiplexer #(.enable("false")) multiplexer_3 (.in0(rs[13]), .in1(rs[12]), .out(multiplexer_3_out));  // open: sel
  Multiplexer #(.enable("false")) multiplexer_4 (.in0(rs[12]), .in1(rs[11]), .out(multiplexer_4_out));  // open: sel
  Multiplexer #(.enable("false")) multiplexer_5 (.in0(rs[11]), .in1(rs[10]), .out(multiplexer_5_out));  // open: sel
  Multiplexer #(.enable("false")) multiplexer_6 (.in0(rs[10]), .in1(rs[9]), .out(multiplexer_6_out));  // open: sel
  Multiplexer #(.enable("false")) multiplexer_7 (.in0(rs[9]), .in1(rs[8]), .out(multiplexer_7_out));  // open: sel
  Multiplexer #(.enable("false")) multiplexer_8 (.in0(rs[8]), .in1(rs[7]), .out(multiplexer_8_out));  // open: sel
  Multiplexer #(.enable("false")) multiplexer_9 (.in0(rs[7]), .in1(rs[6]), .out(multiplexer_9_out));  // open: sel
  Multiplexer #(.enable("false")) multiplexer_10 (.in0(rs[6]), .in1(rs[5]), .out(multiplexer_10_out));  // open: sel
  Multiplexer #(.enable("false")) multiplexer_11 (.in0(rs[5]), .in1(rs[4]), .out(multiplexer_11_out));  // open: sel
  Multiplexer #(.enable("false")) multiplexer_12 (.in0(rs[4]), .in1(rs[3]), .out(multiplexer_12_out));  // open: sel
  Multiplexer #(.enable("false")) multiplexer_13 (.in0(rs[3]), .in1(rs[2]), .out(multiplexer_13_out));  // open: sel
  Multiplexer #(.enable("false")) multiplexer_14 (.in0(rs[2]), .in1(rs[1]), .out(multiplexer_14_out));  // open: sel
  Multiplexer #(.enable("false")) multiplexer_15 (.in0(rs[1]), .in1(rs[0]), .out(multiplexer_15_out));  // open: sel
  Multiplexer #(.enable("false")) multiplexer_16 (.in0(rs[0]), .in1(1'b0), .out(multiplexer_16_out));  // open: sel
  Multiplexer #(.enable("false")) multiplexer_17 (
    .in0(multiplexer_1_out), .in1(multiplexer_3_out), .out(multiplexer_17_out));  // open: sel
  Multiplexer #(.enable("false")) multiplexer_18 (
    .in0(multiplexer_2_out), .in1(multiplexer_4_out), .out(multiplexer_18_out));  // open: sel
  Multiplexer #(.enable("false")) multiplexer_19 (
    .in0(multiplexer_3_out), .in1(multiplexer_5_out), .out(multiplexer_19_out));  // open: sel
  Multiplexer #(.enable("false")) multiplexer_20 (
    .in0(multiplexer_4_out), .in1(multiplexer_6_out), .out(multiplexer_20_out));  // open: sel
  Multiplexer #(.enable("false")) multiplexer_21 (
    .in0(multiplexer_5_out), .in1(multiplexer_7_out), .out(multiplexer_21_out));  // open: sel
  Multiplexer #(.enable("false")) multiplexer_22 (
    .in0(multiplexer_6_out), .in1(multiplexer_8_out), .out(multiplexer_22_out));  // open: sel
  Multiplexer #(.enable("false")) multiplexer_23 (
    .in0(multiplexer_7_out), .in1(multiplexer_9_out), .out(multiplexer_23_out));  // open: sel
  Multiplexer #(.enable("false")) multiplexer_24 (
    .in0(multiplexer_8_out), .in1(multiplexer_10_out), .out(multiplexer_24_out));  // open: sel
  Multiplexer #(.enable("false")) multiplexer_25 (
    .in0(multiplexer_9_out), .in1(multiplexer_11_out), .out(multiplexer_25_out));  // open: sel
  Multiplexer #(.enable("false")) multiplexer_26 (
    .in0(multiplexer_10_out), .in1(multiplexer_12_out), .out(multiplexer_26_out));  // open: sel
  Multiplexer #(.enable("false")) multiplexer_27 (
    .in0(multiplexer_11_out), .in1(multiplexer_13_out), .out(multiplexer_27_out));  // open: sel
  Multiplexer #(.enable("false")) multiplexer_28 (
    .in0(multiplexer_12_out), .in1(multiplexer_14_out), .out(multiplexer_28_out));  // open: sel
  Multiplexer #(.enable("false")) multiplexer_29 (
    .in0(multiplexer_13_out), .in1(multiplexer_15_out), .out(multiplexer_29_out));  // open: sel
  Multiplexer #(.enable("false")) multiplexer_30 (
    .in0(multiplexer_14_out), .in1(multiplexer_16_out), .out(multiplexer_30_out));  // open: sel
  Multiplexer #(.enable("false")) multiplexer_31 (
    .in0(multiplexer_15_out), .in1(1'b0), .out(multiplexer_31_out));  // open: sel
  Multiplexer #(.enable("false")) multiplexer_32 (
    .in0(multiplexer_16_out), .in1(1'b0), .out(multiplexer_29_out));  // open: sel
  Multiplexer #(.enable("false")) multiplexer_33 (.in0(multiplexer_29_out), .in1(1'b0), .out(slout[12]));  // open: sel
  Multiplexer #(.enable("false")) multiplexer_34 (.in0(multiplexer_30_out), .in1(1'b0), .out(slout[13]));  // open: sel
  Multiplexer #(.enable("false")) multiplexer_35 (.in0(multiplexer_31_out), .in1(1'b0), .out(slout[14]));  // open: sel
  Multiplexer #(.enable("false")) multiplexer_36 (.in0(multiplexer_29_out), .in1(1'b0), .out(slout[15]));  // open: sel
  Multiplexer #(.enable("false")) multiplexer_37 (
    .in0(multiplexer_17_out), .in1(multiplexer_21_out), .out(slout[0]));  // open: sel
  Multiplexer #(.enable("false")) multiplexer_38 (
    .in0(multiplexer_18_out), .in1(multiplexer_22_out), .out(slout[1]));  // open: sel
  Multiplexer #(.enable("false")) multiplexer_39 (
    .in0(multiplexer_19_out), .in1(multiplexer_23_out), .out(slout[2]));  // open: sel
  Multiplexer #(.enable("false")) multiplexer_40 (
    .in0(multiplexer_20_out), .in1(multiplexer_24_out), .out(slout[3]));  // open: sel
  Multiplexer #(.enable("false")) multiplexer_41 (
    .in0(multiplexer_21_out), .in1(multiplexer_25_out), .out(slout[4]));  // open: sel
  Multiplexer #(.enable("false")) multiplexer_42 (
    .in0(multiplexer_22_out), .in1(multiplexer_26_out), .out(slout[5]));  // open: sel
  Multiplexer #(.enable("false")) multiplexer_43 (
    .in0(multiplexer_23_out), .in1(multiplexer_27_out), .out(slout[6]));  // open: sel
  Multiplexer #(.enable("false")) multiplexer_44 (
    .in0(multiplexer_24_out), .in1(multiplexer_28_out), .out(slout[7]));  // open: sel
  Multiplexer #(.enable("false")) multiplexer_45 (
    .in0(multiplexer_25_out), .in1(multiplexer_29_out), .out(slout[8]));  // open: sel
  Multiplexer #(.enable("false")) multiplexer_46 (
    .in0(multiplexer_26_out), .in1(multiplexer_30_out), .out(slout[9]));  // open: sel
  Multiplexer #(.enable("false")) multiplexer_47 (
    .in0(multiplexer_27_out), .in1(multiplexer_31_out), .out(slout[10]));  // open: sel
  Multiplexer #(.enable("false")) multiplexer_48 (
    .in0(multiplexer_28_out), .in1(multiplexer_29_out), .out(slout[11]));  // open: sel

  // Other names for the same wires on the sheet: b1 = rs[0]; b2 = rs[1]; b3 = rs[2]; b4 = rs[3]; b5 = rs[4];
  //   b6 = rs[5]; b7 = rs[6]; b8 = rs[7]; b9 = rs[8]; b10 = rs[9]; b11 = rs[10]; b12 = rs[11]; b13 = rs[12];
  //   b14 = rs[13]; b15 = rs[14]; b16 = rs[15]; out16 = slout[0]; out15 = slout[1]; out14 = slout[2];
  //   out13 = slout[3]; out12 = slout[4]; out11 = slout[5]; out10 = slout[6]; out9 = slout[7]; out8 = slout[8];
  //   out7 = slout[9]; out6 = slout[10]; out5 = slout[11]; out4 = slout[12]; out3 = slout[13]; out2 = slout[14];
  //   out1 = slout[15]
endmodule

module shift1left (
  input  [15:0] inreg,
  output [15:0] outreg
);


  assign outreg = {inreg[14:0], 1'b0};
endmodule

module barrelleftshift (
  input  [2:0] shamt,
  input  [15:0] inputreg,
  output [15:0] outreg
);

  wire [15:0] multiplexer_1_out, multiplexer_2_out, shift1left_1_outreg, shift2left_1_outreg,
       shift4left_1_outreg;

  shift1left shift1left_1 (.inreg(inputreg), .outreg(shift1left_1_outreg));
  Multiplexer #(.width(16), .enable("false")) multiplexer_1 (
    .in0(inputreg), .in1(shift1left_1_outreg), .out(multiplexer_1_out), .sel(shamt[0]));
  Multiplexer #(.width(16), .enable("false")) multiplexer_2 (
    .in0(multiplexer_1_out), .in1(shift2left_1_outreg), .out(multiplexer_2_out), .sel(shamt[1]));
  shift2left shift2left_1 (.inreg(multiplexer_1_out), .outreg(shift2left_1_outreg));
  shift4left shift4left_1 (.inreg(multiplexer_2_out), .outreg(shift4left_1_outreg));
  Multiplexer #(.width(16), .enable("false")) multiplexer_3 (
    .in0(multiplexer_2_out), .in1(shift4left_1_outreg), .out(outreg), .sel(shamt[2]));

  // Other names for the same wires on the sheet: inreg[15:0] = inputreg; shamt1 = shamt[0]; shamt2 = shamt[1];
  //   shamt3 = shamt[2]
endmodule

module shift2left (
  input  [15:0] inreg,
  output [15:0] outreg
);


  assign outreg = {inreg[13:0], 2'b00};
endmodule

module shift4left (
  input  [15:0] inreg,
  output [15:0] outreg
);


  assign outreg = {inreg[11:0], 4'b0000};
endmodule

module shift1right (
  input  [15:0] inreg,
  output [15:0] outreg
);


  assign outreg = {1'b0, inreg[15:1]};
endmodule

module shift2right (
  input  [15:0] inreg,
  output [15:0] outreg
);


  assign outreg = {2'b00, inreg[15:2]};
endmodule

module shift4right (
  input  [15:0] inreg,
  output [15:0] outreg
);


  assign outreg = {4'b0000, inreg[15:4]};
endmodule

module barrelright (
  input  [2:0] shamt,
  input  [15:0] inputreg,
  output [15:0] outreg
);

  wire [15:0] multiplexer_1_out, multiplexer_2_out, shift1right_1_outreg, shift2right_1_outreg,
       shift4right_1_outreg;

  shift1right shift1right_1 (.inreg(inputreg), .outreg(shift1right_1_outreg));
  Multiplexer #(.width(16), .enable("false")) multiplexer_1 (
    .in0(inputreg), .in1(shift1right_1_outreg), .out(multiplexer_1_out), .sel(shamt[0]));
  Multiplexer #(.width(16), .enable("false")) multiplexer_2 (
    .in0(multiplexer_1_out), .in1(shift2right_1_outreg), .out(multiplexer_2_out), .sel(shamt[1]));
  shift2right shift2right_1 (.inreg(multiplexer_1_out), .outreg(shift2right_1_outreg));
  shift4right shift4right_1 (.inreg(multiplexer_2_out), .outreg(shift4right_1_outreg));
  Multiplexer #(.width(16), .enable("false")) multiplexer_3 (
    .in0(multiplexer_2_out), .in1(shift4right_1_outreg), .out(outreg), .sel(shamt[2]));

  // Other names for the same wires on the sheet: inreg[15:0] = inputreg; shamt1 = shamt[0]; shamt2 = shamt[1];
  //   shamt3 = shamt[2]
endmodule

module memorylatch (
  input  [15:0] address,
  input  WE,
  input  clk,
  input  [15:0] data_in,
  output [15:0] address_latched,
  output WE_latched,
  output OE_latched,
  output [15:0] data_in_latched
);

  wire DMwe_latch_q;
  wire [15:0] addr_latch_q;

  Register #(.width(16), .trigger("falling")) addr_latch (
    .D(address), .en(WE), .clk(clk), .Q(addr_latch_q));  // open: clr
  D_Flip_Flop #(.trigger("falling")) DMwe_latch (.D(WE), .clk(clk), .Q(DMwe_latch_q));  // open: Qn, preset, reset
  Register #(.width(16), .trigger("falling")) data_to_be_written (
    .D(data_in), .en(WE), .clk(clk), .Q(data_in_latched));  // open: clr
  Multiplexer #(.width(16), .enable("false")) multiplexer_1 (
    .in0(address), .in1(addr_latch_q), .out(address_latched), .sel(DMwe_latch_q));
  and and_1 (WE_latched, clk, DMwe_latch_q);
  not not_1 (OE_latched, WE_latched);
endmodule
